# Fritzing sketch connect_to_pi (saved by Fritzing 0.8.7b)
breadboards: 1

parts:
  Raspberry_Pi_B_rev1 = Raspberry Pi B rev2
  U1 = RF-LINK_TX [package=rf-link_tx]

nets:
  N1: Raspberry_Pi_B_rev1.5V, U1.DATA
  N2: Raspberry_Pi_B_rev1.GND, U1.ANT
  N3: Raspberry_Pi_B_rev1.GPIO_17, U1.+5V

notes:
  17cm wire used as
  antenna to improve
  range
  RF transmitter/PI:
  VCC - +5V,
  DATA - GPIO #17
  GND - GND
